# Fritzing sketch wearable circuit diagram (saved by Fritzing 0.9.3b)
breadboards: 2

parts:
  U5 = ESP32S-HiLetgo [part_number=ESP32S-HiLetgo]
  M3 = tp5100 [package=THT]
  U6 = LIPO-1000mAh [package=lipo-1000]
  TRM2 = Terminal 2pin
  M4 = MAX30102
  U7 = MLX90614 [package=to-39]
  LCD2 = Waveshare 1.28 inch Round 240x240 LCD Display
  J1 = Piezo Speaker
  S1 = Pushbutton [package="[SMD]"]
  S2 = Pushbutton [package="[SMD]"]

nets:
  VIN: U5.3.3, U5.EN, M3.-IN, M3.-BAT, U6.+, TRM2.pin_2, M4.VIN, U7.VDD, LCD2.pin_1, S1.Pin_3, S1.Pin_4, S2.Pin_3, S2.Pin_4
  N1: U5.GPIO34, J1.pin2
  GND: U5.GND, U5.VIN, M3.+BAT, U6.-, TRM2.pin_1, M4.GND, U7.VSS, LCD2.pin2, J1.pin1, S1.Pin_1, S1.Pin_2, S2.Pin_1, S2.Pin_2
  N2: U5.GPIO16, LCD2.pin_7
  N3: U5.GPIO17, LCD2.pin_6
  N4: U5.GPIO5, LCD2.pin_5
  N5: U5.GPIO18, LCD2.pin4
  N6: U5.GPIO19, LCD2.pin_8
  N7: U5.GPIO21, M4.SDA, U7.PWM_SDA
  N8: U5.GPIO1, LCD2.pin3
  N9: U5.GPIO22, M4.SCL, U7.SCL_VZ

custom parts:
  ESP32S-HiLetgo: HiLetgo ESP-WROOM-32 ESP32 ESP-32S Development Board 2.4GHz Dual-Mode WiFi + Bluetooth Dual Cores Microcontroller The ESP32 integrated with Antenna switches, RF Balun, power amplifiers, low-noise amplifiers, filters, and management modules, and the entire solution occupies the least area of PCB. 2.4 GHz Wi-Fi plus Bluetooth dual-mode chip, with TSMC Ultra-low power consumption 40nm technology,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
  tp5100: Tp5100 battery charger module. Generic ebay type.
  Terminal 2pin: 2-pin Terminal Block
  MAX30102: Oximeter module using the MAX30102 chip. You may wish to read (and check your module) this post on power problems with these modules: https://reedpaper.wordpress.com/2018/08/22/pulse-oximeter-max30100-max30102-how-to-fix-wrong-board/ . As usual, if you want the mounting holes in pcb, you need to drag a hole over the pad in silkscreen to actually drill the hole (by default they are not drilled)
  Waveshare 1.28 inch Round 240x240 LCD Display: Waveshare 1.28 inch Round 240x240 LCD Display with GC9A01 Controller
